# Fritzing sketch schematic (saved by Fritzing 0.9.1b)
circuit board: 8.46667cm x 5.64444cm
breadboards: 1

parts:
  R1 = Resistor [tolerance=±5% resistance=220 package=THT]
  R2 = Resistor [tolerance=±5% resistance=220 package=THT]
  R3 = Resistor [tolerance=±5% resistance=220 package=THT]
  R4 = Resistor [tolerance=±5% resistance=220 package=THT]
  U1 = 74HC595 [package="DIP16 [THT]"]
  U2 = ATTiny84 [package=dip]
  Part1 = Real Time Clock Module - DS1307 RTC Breakout Board
  LED5 = smd LED [color="Red (633nm)" package="0603 [SMD]"]
  LED6 = smd LED [color="Red (633nm)" package="0603 [SMD]"]
  LED7 = smd LED [color="Red (633nm)" package="0603 [SMD]"]
  LED8 = smd LED [color="Red (633nm)" package="0603 [SMD]"]
  LED9 = smd LED [color="Red (633nm)" package="0603 [SMD]"]
  LED10 = smd LED [color="Red (633nm)" package="0603 [SMD]"]
  LED12 = smd LED [color="Red (633nm)" package="0603 [SMD]"]
  LED13 = smd LED [color="Red (633nm)" package="0603 [SMD]"]
  LED14 = smd LED [color="Red (633nm)" package="0603 [SMD]"]
  LED15 = smd LED [color="Red (633nm)" package="0603 [SMD]"]
  LED16 = smd LED [color="Red (633nm)" package="0603 [SMD]"]
  LED17 = smd LED [color="Red (633nm)" package="0603 [SMD]"]
  LED18 = smd LED [color="Red (633nm)" package="0603 [SMD]"]
  LED19 = smd LED [color="Red (633nm)" package="0603 [SMD]"]
  LED20 = smd LED [color="Red (633nm)" package="0603 [SMD]"]
  LED21 = smd LED [color="Red (633nm)" package="0603 [SMD]"]
  LED22 = smd LED [color="Red (633nm)" package="0603 [SMD]"]
  LED23 = smd LED [color="Red (633nm)" package="0603 [SMD]"]
  LED24 = smd LED [color="Red (633nm)" package="0603 [SMD]"]
  LED25 = smd LED [color="Red (633nm)" package="0603 [SMD]"]
  Q1 = NPN-Transistor [package="TO92 [THT]"]
  Q2 = NPN-Transistor [package="TO92 [THT]"]
  Q3 = NPN-Transistor [package="TO92 [THT]"]
  Q4 = NPN-Transistor [package="TO92 [THT]"]
  Q5 = NPN-Transistor [package="TO92 [THT]"]
  Q6 = NPN-Transistor [package="TO92 [THT]"]
  R5 = Resistor [tolerance=±5% resistance=10k package=THT]
  R6 = Resistor [tolerance=±5% resistance=10k package=THT]
  R7 = Resistor [tolerance=±5% resistance=10k package=THT]
  R8 = Resistor [tolerance=±5% resistance=10k package=THT]
  R9 = Resistor [tolerance=±5% resistance=10k package=THT]
  R10 = Resistor [tolerance=±5% resistance=10k package=THT]
  C1 = Ceramic Capacitor [capacitance=100nF package="100 mil [THT, multilayer]"]
  C2 = Ceramic Capacitor [capacitance=100nF package="100 mil [THT, multilayer]"]

nets:
  N1: R1.Pin_0, U2.pin13
  N2: R1.Pin_1, LED7.anode, LED18.anode, LED23.anode
  N3: R2.Pin_0, U2.pin12
  N4: R2.Pin_1, LED10.anode, LED14.anode, LED16.anode, LED19.anode, LED21.anode
  N5: R3.Pin_0, U2.pin11
  N6: R3.Pin_1, LED5.anode, LED9.anode, LED15.anode, LED17.anode, LED22.anode, LED25.anode
  N7: R4.Pin_0, U2.pin10
  N8: R4.Pin_1, LED6.anode, LED8.anode, LED12.anode, LED13.anode, LED20.anode, LED24.anode
  N9: U1.Q1, R9.Pin_0
  N10: U1.Q2, R8.Pin_0
  N11: U1.Q3, R7.Pin_0
  N12: U1.Q4, R6.Pin_0
  N13: U1.Q5, R5.Pin_0
  GND: U1.GND, U1.OE, U2.pin14, Part1.GND, Q1.E, Q2.E, Q3.E, Q4.E, Q5.E, Q6.E, C1.1, C2.0
  5V: U1.MR, U1.VCC, U2.pin1, Part1.5V, C1.0, C2.1
  N14: U1.SH_CP, U2.pin4
  N15: U1.ST_CP, U2.pin5
  N16: U1.DS, U2.pin2
  N17: U1.Q0, R10.Pin_0
  N18: U2.pin6, Part1.SDA
  N19: U2.pin7, Part1.SCL
  N20: LED5.cathode, LED6.cathode, Q1.C
  N21: LED7.cathode, LED8.cathode, LED9.cathode, LED10.cathode, Q2.C
  N22: LED12.cathode, LED16.cathode, LED17.cathode, Q3.C
  N23: LED13.cathode, LED14.cathode, LED15.cathode, LED18.cathode, Q4.C
  N24: LED19.cathode, LED22.cathode, LED24.cathode, Q5.C
  N25: LED20.cathode, LED21.cathode, LED23.cathode, LED25.cathode, Q6.C
  N26: Q1.B, R5.Pin_1
  N27: Q2.B, R6.Pin_1
  N28: Q3.B, R7.Pin_1
  N29: Q4.B, R8.Pin_1
  N30: Q5.B, R9.Pin_1
  N31: Q6.B, R10.Pin_1

custom parts:
  ATTiny84: Atmel ATTiny84 processor. 8 ADC pins, 4 PWM pins. Available in either 10MHz or 20MHz. The last 2 pin numbers refer to arduino. D6 = Arduino 6, A6 = Arduino A6 example: PA6 (SDA/MOSI/OC1A/DI/AD6/PCINT6/D6/A6) NOTE: This part is diagrammed to suit the MIT HLT ATTiny84 core at https://github.com/damellis/attiny/
